# Fritzing sketch wiringDiagram (saved by Fritzing 0.9.3b)

parts:
  Part1 = Arduino Uno (Rev3)
  LED1 = LED - 5mm [color="White (4500K)" package="5 mm [THT]"]
  Part2 = Soil Moisture Sensor
  VCC1 = Battery block 9V  # not connected

nets:
  N1: Part1.A0, Part2.SIG
  N2: Part1.D13/SCK, LED1.cathode
  GND: Part1.GND, LED1.anode, Part2.GND
  5V: Part1.5V, Part2.VCC
